# Fritzing sketch fretboard circuit 2 (saved by Fritzing 0.9.3b)
stripboards: 1
perfboards: 2

parts:
  IC1 = DIP - 16 pins [chip_label=4051 package="DIP (Dual Inline) [THT]"]
  J1 = female pin header, 6 pins [form="♀ (female)"]
  J2 = female pin header, 6 pins [form="♀ (female)"]
  IC2 = DIP - 16 pins [chip_label=4051 package="DIP (Dual Inline) [THT]"]
  J3 = female pin header, 6 pins [form="♀ (female)"]
  IC3 = DIP - 16 pins [chip_label=4051 package="DIP (Dual Inline) [THT]"]
  J4 = female pin header, 6 pins [form="♀ (female)"]
  J5 = female alternating pin header, 6 pins [form="♀ (female)"]
  J7 = female pin header, 6 pins [form="♀ (female)"]
  J8 = female pin header, 3 pins [form="♀ (female)"]
  J6 = female pin header, 3 pins [form="♀ (female)"]
  IC4 = DIP - 16 pins [chip_label=4051 package="DIP (Dual Inline) [THT]"]  # not connected
  J10 = female pin header, 6 pins [form="♀ (female)"]  # not connected
  J11 = female pin header, 6 pins [form="♀ (female)"]  # not connected
  IC5 = DIP - 16 pins [chip_label=4051 package="DIP (Dual Inline) [THT]"]  # not connected
  J12 = female pin header, 6 pins [form="♀ (female)"]  # not connected
  IC6 = DIP - 16 pins [chip_label=4051 package="DIP (Dual Inline) [THT]"]  # not connected
  J13 = female pin header, 6 pins [form="♀ (female)"]  # not connected
  J14 = female pin header, 8 pins [form="♀ (female)"]  # not connected
  J9 = female pin header, 5 pins [form="♀ (female)"]  # not connected
  J16 = male pin header, 5 pins [form="♂ (male)"]  # not connected
  IC7 = DIP - 16 pins [chip_label=4051 package="DIP (Dual Inline) [THT]"]  # not connected
  J17 = male pin header, 6 pins [form="♂ (male)"]  # not connected
  J18 = male pin header, 6 pins [form="♂ (male)"]  # not connected
  J19 = male pin header, 6 pins [form="♂ (male)"]  # not connected
  J20 = male pin header, 6 pins [form="♂ (male)"]  # not connected
  IC8 = DIP - 16 pins [chip_label=4051 package="DIP (Dual Inline) [THT]"]  # not connected
  IC9 = DIP - 16 pins [chip_label=4051 package="DIP (Dual Inline) [THT]"]  # not connected
  J21 = male pin header, 8 pins [form="♂ (male)"]  # not connected

nets:
  N1: IC1.pin1, IC1.pin2, IC1.pin6, IC1.pin7, IC1.pin8, IC1.pin9, IC1.pin10, IC1.pin11, IC1.pin15, IC1.pin16, J1.pin1, J1.pin5, J1.pin6, J2.pin3, J2.pin4, J2.pin5, J2.pin6, IC2.pin1, IC2.pin4, IC2.pin5, IC2.pin6, IC2.pin7, IC2.pin8, IC2.pin9, IC2.pin10, IC2.pin11, IC2.pin12, IC2.pin13, IC2.pin16, J3.pin1, J3.pin4, J3.pin5, J3.pin6, IC3.pin1, IC3.pin2, IC3.pin6, IC3.pin7, IC3.pin8, IC3.pin9, IC3.pin10, IC3.pin11, IC3.pin15, IC3.pin16, J4.pin1, J4.pin2, J5.pin1, J5.pin6, J7.pin1, J7.pin6, J8.pin1, J8.pin2, J8.pin3, J6.pin1, J6.pin2, J6.pin3
  N2: IC1.pin3, IC1.pin14, J1.pin2, J2.pin2, IC2.pin3, IC2.pin14, IC3.pin4, IC3.pin13, J4.pin3, J4.pin4, J5.pin2, J5.pin3, J5.pin4, J5.pin5, J7.pin2, J7.pin3, J7.pin4, J7.pin5
  N3: IC1.pin4, IC1.pin13, J1.pin3
  N4: IC1.pin5, IC1.pin12, J1.pin4
  N5: J2.pin1, IC2.pin2, IC2.pin15, J3.pin2
  N6: J3.pin3, IC3.pin3, IC3.pin14
  N7: IC3.pin5, IC3.pin12, J4.pin5, J4.pin6

notes:
  to next board up neck

custom parts:
  DIP - 16 pins: A DIP stand-in part for whatever IC you want. With 16 pins on a 300mil dual inline package (DIP) footprint.
