# Fritzing sketch fretboard circuit (saved by Fritzing 0.9.3b)
stripboards: 1

parts:
  IC1 = DIP - 16 pins [chip_label=4051 package="DIP (Dual Inline) [THT]"]
  J1 = female pin header, 6 pins [form="♀ (female)"]
  J2 = female pin header, 6 pins [form="♀ (female)"]
  IC2 = DIP - 16 pins [chip_label=4051 package="DIP (Dual Inline) [THT]"]
  J3 = female pin header, 6 pins [form="♀ (female)"]
  IC3 = DIP - 16 pins [chip_label=4051 package="DIP (Dual Inline) [THT]"]
  J4 = female pin header, 6 pins [form="♀ (female)"]
  R1 = Resistor [tolerance=±5% resistance=1M package=THT]
  R2 = Resistor [tolerance=±5% resistance=1M package=THT]
  R3 = Resistor [tolerance=±5% resistance=1M package=THT]
  J5 = female pin header, 5 pins [form="♀ (female)"]
  J6 = female pin header, 4 pins [form="♀ (female)"]
  J7 = female pin header, 5 pins [form="♀ (female)"]
  J8 = female pin header, 4 pins [form="♀ (female)"]

nets:
  N1: IC1.pin1, IC1.pin16, J1.pin5, IC2.pin1, IC2.pin16, J3.pin1, IC3.pin1, IC3.pin16, J4.pin1, J5.pin1, J7.pin1
  N2: IC1.pin2, IC1.pin15, J1.pin1, J1.pin6
  N3: IC1.pin3, IC1.pin14, J1.pin2, R1.Pin_1, J5.pin4, J7.pin4
  N4: IC1.pin4, IC1.pin13, J1.pin3, J2.pin3
  N5: IC1.pin5, IC1.pin12, J1.pin4, J2.pin4
  N6: IC1.pin6, IC1.pin7, IC1.pin8, IC1.pin9, IC1.pin10, IC1.pin11, IC2.pin6, IC2.pin7, IC2.pin8, IC2.pin9, IC2.pin10, IC2.pin11, J3.pin6, IC3.pin2, IC3.pin6, IC3.pin7, IC3.pin8, IC3.pin9, IC3.pin10, IC3.pin11, IC3.pin15, J4.pin2, J6.pin1, J6.pin2, J6.pin3, J6.pin4, J8.pin1, J8.pin2, J8.pin3, J8.pin4
  N7: J2.pin1, IC2.pin2, IC2.pin15, J3.pin2
  N8: J2.pin2, IC2.pin3, IC2.pin14, R2.Pin_1, J5.pin3, J7.pin3
  N9: J2.pin5, IC2.pin4, IC2.pin13, J3.pin4
  N10: J2.pin6, IC2.pin5, IC2.pin12, J3.pin5
  N11: J3.pin3, IC3.pin3, IC3.pin14, R3.Pin_1, J5.pin2, J7.pin2
  N12: IC3.pin4, IC3.pin13, J4.pin3, J4.pin4
  N13: IC3.pin5, IC3.pin12, J4.pin5, J4.pin6
  N14: R1.Pin_0, R2.Pin_0, R3.Pin_0, J5.pin5, J7.pin5

custom parts:
  DIP - 16 pins: A DIP stand-in part for whatever IC you want. With 16 pins on a 300mil dual inline package (DIP) footprint.
