# Fritzing sketch main circuit 2 (saved by Fritzing 0.9.3b)
perfboards: 1

parts:
  Teensy1 = Teensy 3.6 (Basic)
  IC1 = DIP - 16 pins [chip_label="4051 (frets)" package="DIP (Dual Inline) [THT]"]  # not connected
  IC2 = DIP - 16 pins [chip_label="4051 (strings)" package="DIP (Dual Inline) [THT]"]  # not connected
  IC3 = DIP - 16 pins [chip_label="4051 (knobs 1)" package="DIP (Dual Inline) [THT]"]  # not connected
  IC4 = DIP - 16 pins [chip_label="4051 (knobs 2)" package="DIP (Dual Inline) [THT]"]  # not connected
  IC5 = DIP - 16 pins [chip_label="4051 (knobs 3)" package="DIP (Dual Inline) [THT]"]  # not connected
  IC6 = DIP - 16 pins [chip_label="4051 (switches)" package="DIP (Dual Inline) [THT]"]  # not connected
  IC7 = DIP - 16 pins [chip_label="4051 (palm)" package="DIP (Dual Inline) [THT]"]  # not connected
  IC8 = DIP - 16 pins [chip_label="4051 (knobs 4)" package="DIP (Dual Inline) [THT]"]  # not connected
  J3 = female pin header, 3 pins [form="♀ (female)"]  # not connected
  J4 = female pin header, 4 pins [form="♀ (female)"]  # not connected
  J5 = female pin header, 4 pins [form="♀ (female)"]  # not connected
  J6 = female pin header, 4 pins [form="♀ (female)"]  # not connected
  J7 = female pin header, 4 pins [form="♀ (female)"]  # not connected
  J8 = female pin header, 4 pins [form="♀ (female)"]  # not connected
  J9 = female pin header, 4 pins [form="♀ (female)"]  # not connected
  J2 = female pin header, 8 pins [form="♀ (female)"]  # not connected
  J1 = female pin header, 8 pins [form="♀ (female)"]  # not connected
  J11 = female pin header, 8 pins [form="♀ (female)"]  # not connected
  J12 = female pin header, 8 pins [form="♀ (female)"]  # not connected
  J10 = female pin header, 8 pins [form="♀ (female)"]  # not connected
  J13 = female pin header, 7 pins [form="♀ (female)"]  # not connected
  R1 = Resistor [tolerance=±5% resistance=1k package=THT]  # not connected
  R2 = Resistor [tolerance=±5% resistance=1k package=THT]  # not connected
  R3 = Resistor [tolerance=±5% resistance=1k package=THT]  # not connected
  R4 = Resistor [tolerance=±5% resistance=10k package=THT]  # not connected

nets:
  GND: Teensy1.GND, Teensy1.GND1
  N1: Teensy1.3V3, Teensy1.3V3_1

notes:
  teensy audio board
  leave space for headphones
  15-pin connection to neck -->
  leave space for USB connection

custom parts:
  Teensy 3.6 (Basic): The Teensy is a complete USB-based microcontoller development system, in a very small footprint, capable of implementing many types of projects. All programming is done via the USB port. No special programmer is needed, only a standard micro-USB cable and a PC or Macintosh with a USB port.
  DIP - 16 pins: A DIP stand-in part for whatever IC you want. With 16 pins on a 300mil dual inline package (DIP) footprint.
