# Fritzing sketch main circuit (saved by Fritzing 0.9.3b)
stripboards: 1

parts:
  Teensy1 = Teensy 3.6 (Basic)
  IC1 = DIP - 16 pins [chip_label="4051 (frets)" package="DIP (Dual Inline) [THT]"]
  IC2 = DIP - 16 pins [chip_label="4051 (strings)" package="DIP (Dual Inline) [THT]"]
  IC3 = DIP - 16 pins [chip_label="4051 (knobs 1)" package="DIP (Dual Inline) [THT]"]
  IC4 = DIP - 16 pins [chip_label="4051 (knobs 2)" package="DIP (Dual Inline) [THT]"]
  IC5 = DIP - 16 pins [chip_label="4051 (knobs 3)" package="DIP (Dual Inline) [THT]"]  # not connected

nets:
  GND: Teensy1.GND, Teensy1.GND1
  N1: Teensy1.D0, Teensy1.3V3, Teensy1.3V3_1, IC2.pin3, IC2.pin14, IC4.pin3, IC4.pin14
  N2: Teensy1.D1, IC1.pin1, IC1.pin16, IC3.pin1, IC3.pin16
  N3: Teensy1.D2, IC1.pin2, IC1.pin15, IC3.pin2, IC3.pin15
  N4: Teensy1.D3, IC1.pin3, IC1.pin14, IC3.pin3, IC3.pin14
  N5: Teensy1.D4, IC1.pin4, IC1.pin13, IC3.pin4, IC3.pin13
  N6: Teensy1.D5, IC1.pin5, IC1.pin12, IC3.pin5, IC3.pin12
  N7: Teensy1.D6, Teensy1.D7, IC1.pin6, IC1.pin7, IC1.pin10, IC1.pin11, IC3.pin6, IC3.pin7, IC3.pin10, IC3.pin11
  N8: Teensy1.D8, IC1.pin8, IC1.pin9, IC3.pin8, IC3.pin9
  N9: Teensy1.D11, IC2.pin1, IC2.pin16, IC4.pin1, IC4.pin16
  N10: Teensy1.D12, IC2.pin2, IC2.pin15, IC4.pin2, IC4.pin15
  N11: Teensy1.D24, IC2.pin4, IC2.pin13, IC4.pin4, IC4.pin13
  N12: Teensy1.D25, IC2.pin5, IC2.pin12, IC4.pin5, IC4.pin12
  N13: Teensy1.D26, IC2.pin6, IC2.pin11, IC4.pin6, IC4.pin11
  N14: Teensy1.D27, IC2.pin7, IC2.pin10, IC4.pin7, IC4.pin10
  N15: Teensy1.D28, IC2.pin8, IC2.pin9, IC4.pin8, IC4.pin9

custom parts:
  Teensy 3.6 (Basic): The Teensy is a complete USB-based microcontoller development system, in a very small footprint, capable of implementing many types of projects. All programming is done via the USB port. No special programmer is needed, only a standard micro-USB cable and a PC or Macintosh with a USB port.
  DIP - 16 pins: A DIP stand-in part for whatever IC you want. With 16 pins on a 300mil dual inline package (DIP) footprint.
