# Fritzing sketch multiplexcapacitance (saved by Fritzing 0.9.3b)
breadboards: 1

parts:
  IC1 = IC, DIP package, 18 pins [chip_label=4051]
  Part1 = Arduino Uno (Rev3)
  R1 = Resistor [tolerance=±5% resistance=1M package=THT]
  LED1 = LED - 5mm [color="Blue (430nm)" package="5 mm [THT]"]
  LED2 = LED - 5mm [color="Yellow (595nm)" package="5 mm [THT]"]
  LED3 = LED - 5mm [color="Green (570nm)" package="5 mm [THT]"]
  R2 = Resistor [tolerance=±5% resistance=470k package=THT]
  R3 = Resistor [tolerance=±5% resistance=470k package=THT]
  R4 = Resistor [tolerance=±5% resistance=470k package=THT]
  S1 = Pushbutton [package="[THT]"]
  R5 = Resistor [tolerance=±5% resistance=10k package=THT]

nets:
  N1: IC1.pin3, Part1.D3_PWM, R1.Pin_1
  N2: IC1.pin7, IC1.pin8, IC1.pin9, Part1.GND, LED1.cathode, LED2.cathode, LED3.cathode, R5.Pin_0
  N3: IC1.pin10, Part1.D6_PWM
  N4: IC1.pin11, Part1.D5_PWM
  N5: IC1.pin12, Part1.D4
  N6: IC1.pin18, Part1.5V, S1.Pin_1, S1.Pin_2
  N7: Part1.D8, R2.Pin_0
  N8: Part1.D9_PWM, R3.Pin_0
  N9: Part1.D10_PWM/SS, R4.Pin_0
  N10: Part1.D11_PWM/MOSI, S1.Pin_3, S1.Pin_4, R5.Pin_1
  N11: Part1.D2, R1.Pin_0
  N12: LED1.anode, R2.Pin_1
  N13: LED2.anode, R3.Pin_1
  N14: LED3.anode, R4.Pin_1

notes:
  Touch fingers to ends of wires to light LEDs
